// Digital circuit MikroLeo_v0.19.dig as structural Verilog
module MikroLeo_v0_19 (
  input  FREQ,
  input  AUTO,
  input  INA3,
  input  in_4,
  input  in_5,
  input  INA0,
  input  INB3,
  input  in_8,
  input  in_9,
  input  INB0,
  input  INC3,
  input  in_12,
  input  in_13,
  input  INC0,
  input  IND3,
  input  in_16,
  input  in_17,
  input  IND0
);

  wire _7474_1_p11, _7474_1_p12, AL0, AL1, AL2, AL3, AMODE, and_1_out, and_2_out, and_6_out, and_7_out,
       and_8_out, and_9_out, and_10_out, and_14_out, and_17_out, ARITH__nNAND, Arithmetic_Operation_p12,
       Arithmetic_Operation_p13, Arithmetic_Operation_p14, Arithmetic_Operation_p15, bussplitter_1_d4,
       bussplitter_1_d5, bussplitter_1_d6, bussplitter_1_d7, button_1_out, button_2_out, button_3_out,
       button_4_out, button_5_out, button_6_out, button_7_out, button_8_out, button_9_out, button_10_out,
       button_11_out, button_12_out, button_13_out, button_14_out, button_15_out, button_16_out, C, CARRY,
       CLK, CLKN, CLOCKACC, d_ff_1_nq, d_ff_2_nq, d_ff_3_nq, d_ff_4_nq, d_ff_5_nq, d_ff_6_nq, d_ff_7_nq,
       d_ff_8_nq, d_ff_9_nq, d_ff_10_nq, d_ff_11_nq, d_ff_12_nq, d_ff_13_nq, d_ff_14_nq, d_ff_15_nq,
       d_ff_16_nq, DATATOREG2, diodebackward_1_out, diodeforward_3_out, diodeforward_5_out,
       diodeforward_7_out, diodeforward_9_out, diodeforward_11_out, diodeforward_13_out, diodeforward_15_out,
       diodeforward_17_out, I0, I1, I2, I3, I4, I5, I6, I7, I8, I9, I10, I11, I12, I13, I14, I15, JPC, JPZ,
       MICRO2_IN, MOD0, MOD1, MUX1_p13, MUX1_p14, MUX1_p15, MUX1_p16, nACCn, nACCRA, nACCRAM, nACCRB,
       nACCTOALU, nACCTOREGIN, nand_1_out, nand_2_out, nand_3_out, nand_4_out, nand_5_out, nand_6_out,
       nCLOCKACCEN, nDATATOREG, nENDATABUSTOREGIN, nINAOE, nINBOE, nINCOE, nINDOE, nINxOE, nLDIACCn,
       nLOADADDRC, nMD0, nMD1, nMD2, nMD3, not_1_out, not_2_out, not_3_out, not_5_out, not_7_out, not_8_out,
       not_9_out, not_10_out, not_11_out, not_12_out, not_13_out, not_14_out, not_16_out, not_17_out,
       not_19_out, not_20_out, nOUTx, nOUTxn, nOUTxRA, nOUTxRAM, nPRG, nRALE, nRAOE, nRBLE, nRBOE, nRCLE,
       nRCOE, nRE, nROMOE, nRSTPC, nSOURCEB, nWE, nWE_ROM, OE_ROM, or_1_out, or_3_out, or_4_out, or_5_out,
       or_6_out, PCL_p12, PCM_p12, Program_p3, pullup_5_out, PWONRST_2_out, PWONRST_out, RST, RST_out,
       STEP_out, Stepf, TRIGGERRSTPC, Z, ZERO;
  wire [2:0] dPCH;
  wire [3:0] ACC, DBUSTOREGIN, dOUTA, dOUTB, dOUTC, dOUTD, dPCL, dPCM, dPRG__HiNB, dPRG__MAddr, dPRG__MICRO,
       dPRG__OPR, LA_3_0, MA_7_4, MAddr, MICRO, MUX2_p9, MUX2_p15, OPR, RA, RB, RC, xor_4_out;
  wire [7:0] _6116_d;

  Seven_Seg_Hex seven_seg_hex_1 (.d(dOUTD), .dp(1'b0));
  LED led_1 (.in(I0));
  LED led_2 (.in(I14));
  Seven_Seg_Hex seven_seg_hex_2 (.d(dOUTC), .dp(1'b0));
  LED led_3 (.in(I1));
  LED led_4 (.in(I15));
  LED led_5 (.in(I2));
  Seven_Seg_Hex seven_seg_hex_3 (.d(dOUTB), .dp(1'b0));
  LED led_6 (.in(I3));
  Seven_Seg_Hex seven_seg_hex_4 (.d(dOUTA), .dp(1'b0));
  LED led_7 (.in(I4));
  LED led_8 (.in(I5));
  Button STEP (.out(STEP_out));
  or or_1 (or_1_out, STEP_out, Stepf);
  LED led_9 (.in(I6));
  and and_1 (and_1_out, FREQ, AUTO);
  and and_2 (and_2_out, not_1_out, or_1_out);
  not not_1 (not_1_out, AUTO);
  Seven_Seg_Hex seven_seg_hex_5 (.d(ACC), .dp(1'b0));
  LED led_10 (.in(I7));
  LED led_11 (.in(nINAOE));
  // _74173 _74173_1: pin names not known; wires that end beside it: 1'b0, 1'b0, I9, I9, CLK, DBUSTOREGIN[3], DBUSTOREGIN[2], DBUSTOREGIN[1], RST, dOUTD[3], 1'b0, dOUTD[2], 1'b1, dOUTD[1], DBUSTOREGIN[0], dOUTD[0], 1'b0, 1'b0, I6, I6
  LED led_12 (.in(I8));
  LED led_13 (.in(nINBOE));
  or or_2 (CLK, and_1_out, and_2_out);
  not not_2 (not_2_out, nCLOCKACCEN);
  Button #(.activeLow("true")) u_RST (.out(RST_out));
  DiodeBackward diodebackward_1 (.in(RST_out), .out(diodebackward_1_out));
  Reset PWONRST (.out(PWONRST_out));
  DiodeBackward diodebackward_2 (.in(PWONRST_out), .out(diodebackward_1_out));
  Seven_Seg_Hex seven_seg_hex_6 (.d(RC), .dp(1'b0));
  LED led_14 (.in(I9));
  LED led_15 (.in(nINCOE));
  not not_3 (not_3_out, CLK);
  not not_4 (nPRG, and_2_out);
  and and_3 (CLOCKACC, CLK, not_2_out);
  PullUp pullup_1 (.out(diodebackward_1_out));
  not not_5 (not_5_out, TRIGGERRSTPC);
  // _74157 MUX4: pin names not known; wires that end beside it: AMODE, OPR[0], OPR[1], OPR[2], OPR[3], RA[0], RA[1], RA[2], RA[3], MICRO2_IN, 1'b1, 1'b0, LA_3_0[0], LA_3_0[1], LA_3_0[2], LA_3_0[3]
  // _74157 MUX3: pin names not known; wires that end beside it: AMODE, MAddr[0], MAddr[1], MAddr[2], MAddr[3], RB[0], RB[1], RB[2], RB[3], MICRO2_IN, 1'b1, 1'b0, MA_7_4[0], MA_7_4[1], MA_7_4[2], MA_7_4[3]
  LED led_16 (.in(I10));
  LED led_17 (.in(nINDOE));
  and and_4 (CLKN, not_3_out, not_3_out);
  // _7474 _7474_1: pin names not known; wires that end beside it: nRSTPC, nLOADADDRC, CLK, 1'b1, nRSTPC, I12, CLK, 1'b1, 1'b1, 1'b0, _7474_1_p11, _7474_1_p12
  not not_6 (RST, diodebackward_1_out);
  and and_5 (nRSTPC, diodebackward_1_out, not_5_out);
  Seven_Seg_Hex seven_seg_hex_7 (.d(RB), .dp(1'b0));
  LED led_18 (.in(I11));
  and and_6 (and_6_out, nLOADADDRC, _7474_1_p11);
  and and_7 (and_7_out, _7474_1_p12, I12);
  // _74173 _74173_2: pin names not known; wires that end beside it: CLK, DBUSTOREGIN[3], DBUSTOREGIN[2], DBUSTOREGIN[1], RST, dOUTC[3], 1'b0, dOUTC[2], 1'b1, dOUTC[1], DBUSTOREGIN[0], dOUTC[0], 1'b0, 1'b0, I5, I5
  Seven_Seg_Hex seven_seg_hex_8 (.d(RA), .dp(1'b0));
  LED led_19 (.in(I12));
  LED led_20 (.in(CARRY));
  LED led_21 (.in(I13));
  LED led_22 (.in(ZERO));
  and and_8 (and_8_out, and_6_out, and_7_out);
  Seven_Seg_Hex seven_seg_hex_9 (.d({1'b0, dPCH}), .dp(1'b0));
  LED led_23 (.in(MICRO2_IN));
  LED led_24 (.in(nROMOE));
  and and_9 (and_9_out, I11, I8);
  LED led_25 (.in(nACCTOALU));
  not not_7 (not_7_out, and_9_out);
  // _74173 _74173_3: pin names not known; wires that end beside it: CLK, DBUSTOREGIN[3], DBUSTOREGIN[2], DBUSTOREGIN[1], RST, dOUTB[3], 1'b0, dOUTB[2], 1'b1, dOUTB[1], DBUSTOREGIN[0], dOUTB[0], 1'b0, 1'b0, I4, I4
  Seven_Seg_Hex seven_seg_hex_10 (.d(dPCM), .dp(1'b0));
  LED led_26 (.in(AMODE));
  LED led_27 (.in(nACCTOREGIN));
  // _74161 PCL: pin names not known; wires that end beside it: and_8_out, nRSTPC, CLKN, 1'b1, 1'b1, LA_3_0[0], LA_3_0[1], LA_3_0[2], LA_3_0[3], 1'b1, 1'b0, PCL_p12, dPCL[0], dPCL[1], dPCL[2], dPCL[3]
  // _74161 PCM: pin names not known; wires that end beside it: and_8_out, nRSTPC, CLKN, PCL_p12, 1'b1, MA_7_4[0], MA_7_4[1], MA_7_4[2], MA_7_4[3], 1'b1, 1'b0, PCM_p12, dPCM[0], dPCM[1], dPCM[2], dPCM[3]
  // _74161 PCH: pin names not known; wires that end beside it: and_7_out, nRSTPC, CLKN, PCM_p12, 1'b1, RC[0], RC[1], RC[2], RC[3], 1'b1, 1'b0, dPCH[0], dPCH[1], dPCH[2], TRIGGERRSTPC
  Seven_Seg_Hex seven_seg_hex_11 (.d(dPCL), .dp(1'b0));
  LED led_28 (.in(MOD1));
  LED led_29 (.in(nRALE));
  // _74157 MUX2: pin names not known; wires that end beside it: nRE, DBUSTOREGIN[0], DBUSTOREGIN[1], DBUSTOREGIN[2], DBUSTOREGIN[3], MUX2_p9[0], MUX2_p9[1], MUX2_p9[2], MUX2_p9[3], 1'b0, 1'b1, 1'b0, MUX2_p15[0], MUX2_p15[1], MUX2_p15[2], MUX2_p15[3]
  // _74244 _74244_1: pin names not known; wires that end beside it: INA0, nINAOE, in_5, in_4, INA3, INB0, nINBOE, in_9, in_8, INB3, 1'b1, 1'b0, MUX2_p9[0], MUX2_p9[1], MUX2_p9[2], MUX2_p9[3], MUX2_p9[0], MUX2_p9[1], MUX2_p9[2], MUX2_p9[3]
  // _74244 _74244_2: pin names not known; wires that end beside it: INC0, nINCOE, in_13, in_12, INC3, IND0, nINDOE, in_17, in_16, IND3, 1'b1, 1'b0, MUX2_p9[0], MUX2_p9[1], MUX2_p9[2], MUX2_p9[3], MUX2_p9[0], MUX2_p9[1], MUX2_p9[2], MUX2_p9[3]
  LED led_30 (.in(MOD0));
  LED led_31 (.in(nRAOE));
  LED led_32 (.in(nRCLE));
  xor xor_1 (xor_4_out[0], MUX2_p15[0], not_7_out);
  xor xor_2 (xor_4_out[1], MUX2_p15[1], not_7_out);
  xor xor_3 (xor_4_out[2], MUX2_p15[2], not_7_out);
  xor xor_4 (xor_4_out[3], MUX2_p15[3], not_7_out);
  Seven_Seg_Hex seven_seg_hex_12 (.d(MICRO), .dp(1'b0));
  LED led_33 (.in(nRCOE));
  // _74173 _74173_4: pin names not known; wires that end beside it: CLK, DBUSTOREGIN[3], DBUSTOREGIN[2], DBUSTOREGIN[1], RST, dOUTA[3], 1'b0, dOUTA[2], 1'b1, dOUTA[1], DBUSTOREGIN[0], dOUTA[0]
  Seven_Seg_Hex seven_seg_hex_13 (.d(MAddr), .dp(1'b0));
  LED led_34 (.in(nRE));
  LED led_35 (.in(nWE));
  PullDown pulldown_1 (.out(AL3));
  PullDown pulldown_2 (.out(AL2));
  PullDown pulldown_3 (.out(AL1));
  PullDown pulldown_4 (.out(AL0));
  not not_8 (not_8_out, I10);
  Seven_Seg_Hex seven_seg_hex_14 (.d(OPR), .dp(1'b0));
  or or_3 (or_3_out, nWE_ROM, nPRG);
  // _74283 Arithmetic_Operation: pin names not known; wires that end beside it: not_7_out, xor_4_out[0], xor_4_out[1], xor_4_out[2], xor_4_out[3], AL0, AL1, AL2, AL3, 1'b1, 1'b0, Arithmetic_Operation_p12, Arithmetic_Operation_p13, Arithmetic_Operation_p14, Arithmetic_Operation_p15, C
  nand nand_1 (nand_1_out, AL0, MUX2_p15[0]);
  nand nand_2 (nand_2_out, AL1, MUX2_p15[1]);
  nand nand_3 (nand_3_out, AL2, MUX2_p15[2]);
  nand nand_4 (nand_4_out, AL3, MUX2_p15[3]);
  not not_9 (not_9_out, not_8_out);
  PullUp pullup_2 (.out(or_3_out));
  PullUp pullup_3 (.out(OE_ROM));
  assign MUX2_p9[3] = not_11_out ? RA[3] : 1'bz;  // Driver driver_1
  Reset #(.invertOutput("false")) PWONRST_2 (.out(PWONRST_2_out));
  PullUp pullup_4 (.out(or_3_out));
  // _74173 _74173_5: pin names not known; wires that end beside it: C, 1'b1, 1'b0, RST, Z, 1'b0, 1'b0, CLOCKACC, 1'b0, 1'b0, 1'b0, 1'b0, CARRY, ZERO
  assign MUX2_p9[1] = not_11_out ? RA[1] : 1'bz;  // Driver driver_2
  assign MUX2_p9[2] = not_11_out ? RA[2] : 1'bz;  // Driver driver_3
  assign DBUSTOREGIN[3] = not_10_out ? ACC[3] : 1'bz;  // Driver driver_4
  not not_10 (not_10_out, not_9_out);
  EEPROM #(.AddrBits(11), .isProgramMemory("true"), .Bits(8)) Micro1 (
    .A({dPCH, dPCM, dPCL}), .CS(~PWONRST_2_out), .WE(~or_3_out), .OE(~OE_ROM), .D({MAddr, OPR}));
  EEPROM #(.AddrBits(11), .isProgramMemory("true"), .Bits(8)) Micro2 (
    .A({dPCH, dPCM, dPCL}), .CS(~PWONRST_2_out), .WE(~or_3_out), .OE(~OE_ROM),
    .D({MICRO2_IN, AMODE, MOD1, MOD0, MICRO}));
  // _74173 RA: pin names not known; wires that end beside it: 1'b0, 1'b0, 1'b0, nRALE, CLK, DBUSTOREGIN[3], DBUSTOREGIN[2], DBUSTOREGIN[1], RST, RA[3], 1'b0, RA[2], 1'b1, RA[1], DBUSTOREGIN[0], RA[0], 1'b0, 1'b0, 1'b0
  assign MUX2_p9[0] = not_11_out ? RA[0] : 1'bz;  // Driver driver_5
  assign DBUSTOREGIN[1] = not_10_out ? ACC[1] : 1'bz;  // Driver driver_6
  assign DBUSTOREGIN[2] = not_10_out ? ACC[2] : 1'bz;  // Driver driver_7
  not not_11 (not_11_out, nRAOE);
  assign DBUSTOREGIN[0] = not_10_out ? ACC[0] : 1'bz;  // Driver driver_8
  assign MICRO2_IN = OE_ROM ? dPRG__HiNB[3] : 1'bz;  // Driver driver_9
  LED led_36 (.in(dPRG__HiNB[3]));
  D_FF d_ff_1 (.D(d_ff_1_nq), .C(button_1_out), .Q(dPRG__HiNB[3]), .nQ(d_ff_1_nq));
  Button button_1 (.out(button_1_out));
  not not_12 (not_12_out, I8);
  assign AMODE = OE_ROM ? dPRG__HiNB[2] : 1'bz;  // Driver driver_10
  LED led_37 (.in(dPRG__HiNB[2]));
  D_FF d_ff_2 (.D(d_ff_2_nq), .C(button_2_out), .Q(dPRG__HiNB[2]), .nQ(d_ff_2_nq));
  Button button_2 (.out(button_2_out));
  // _74157 MUX1: pin names not known; wires that end beside it: ARITH__nNAND, Arithmetic_Operation_p12, Arithmetic_Operation_p13, Arithmetic_Operation_p14, Arithmetic_Operation_p15, nand_1_out, nand_2_out, nand_3_out, nand_4_out, 1'b0, 1'b1, 1'b0, MUX1_p13, MUX1_p14, MUX1_p15, MUX1_p16
  // _74173 ACC: pin names not known; wires that end beside it: MUX1_p13, 1'b1, 1'b0, RST, MUX1_p14, MUX1_p15, MUX1_p16, CLOCKACC, not_12_out, 1'b0, 1'b0, 1'b0, ACC[0], ACC[1], ACC[2], ACC[3]
  assign MUX2_p9[2] = not_13_out ? RB[2] : 1'bz;  // Driver driver_11
  assign MUX2_p9[3] = not_13_out ? RB[3] : 1'bz;  // Driver driver_12
  assign MOD1 = OE_ROM ? dPRG__HiNB[1] : 1'bz;  // Driver driver_13
  LED led_38 (.in(dPRG__HiNB[1]));
  D_FF d_ff_3 (.D(d_ff_3_nq), .C(button_3_out), .Q(dPRG__HiNB[1]), .nQ(d_ff_3_nq));
  Button button_3 (.out(button_3_out));
  // _74173 RB: pin names not known; wires that end beside it: nRBLE, CLK, DBUSTOREGIN[3], DBUSTOREGIN[2], DBUSTOREGIN[1], RST, RB[3], 1'b0, RB[2], 1'b1, RB[1], DBUSTOREGIN[0], RB[0], 1'b0, 1'b0, 1'b0
  assign MUX2_p9[0] = not_13_out ? RB[0] : 1'bz;  // Driver driver_14
  assign MUX2_p9[1] = not_13_out ? RB[1] : 1'bz;  // Driver driver_15
  assign MOD0 = OE_ROM ? dPRG__HiNB[0] : 1'bz;  // Driver driver_16
  LED led_39 (.in(dPRG__HiNB[0]));
  D_FF d_ff_4 (.D(d_ff_4_nq), .C(button_4_out), .Q(dPRG__HiNB[0]), .nQ(d_ff_4_nq));
  Button button_4 (.out(button_4_out));
  not not_13 (not_13_out, nRBOE);
  assign MICRO[3] = OE_ROM ? dPRG__MICRO[3] : 1'bz;  // Driver driver_17
  LED led_40 (.in(dPRG__MICRO[3]));
  D_FF d_ff_5 (.D(d_ff_5_nq), .C(button_5_out), .Q(dPRG__MICRO[3]), .nQ(d_ff_5_nq));
  Button button_5 (.out(button_5_out));
  or or_4 (or_4_out, MUX1_p16, MUX1_p15);
  or or_5 (or_5_out, MUX1_p14, MUX1_p13);
  RAMSinglePortSel #(.AddrBits(11), .Bits(8)) _6116 (
    .A({RC[2:0], MA_7_4, LA_3_0}), .CS(~1'b0), .WE(~nWE), .OE(~nRE), .D(_6116_d));
  assign MICRO[2] = OE_ROM ? dPRG__MICRO[2] : 1'bz;  // Driver driver_18
  LED led_41 (.in(dPRG__MICRO[2]));
  D_FF d_ff_6 (.D(d_ff_6_nq), .C(button_6_out), .Q(dPRG__MICRO[2]), .nQ(d_ff_6_nq));
  Button button_6 (.out(button_6_out));
  or or_6 (or_6_out, or_4_out, or_5_out);
  // _74244 BUFFER: pin names not known; wires that end beside it: ACC[0], nACCTOALU, ACC[1], ACC[2], ACC[3], ACC[0], nACCTOREGIN, ACC[1], ACC[2], ACC[3], 1'b1, 1'b0, AL0, AL1, AL2, AL3, DBUSTOREGIN[0], DBUSTOREGIN[1], DBUSTOREGIN[2], DBUSTOREGIN[3]
  assign MUX2_p9[3] = not_16_out ? RC[3] : 1'bz;  // Driver driver_19
  not not_14 (not_14_out, nRE);
  assign MICRO[1] = OE_ROM ? dPRG__MICRO[1] : 1'bz;  // Driver driver_20
  LED led_42 (.in(dPRG__MICRO[1]));
  D_FF d_ff_7 (.D(d_ff_7_nq), .C(button_7_out), .Q(dPRG__MICRO[1]), .nQ(d_ff_7_nq));
  Button button_7 (.out(button_7_out));
  not not_15 (Z, or_6_out);
  assign MUX2_p9[1] = not_16_out ? RC[1] : 1'bz;  // Driver driver_21
  assign MUX2_p9[2] = not_16_out ? RC[2] : 1'bz;  // Driver driver_22
  BusSplitter #(.Bits(8)) bussplitter_1 (
    .D(_6116_d), .OE(not_14_out), .D0(DBUSTOREGIN[0]), .D1(DBUSTOREGIN[1]), .D2(DBUSTOREGIN[2]),
    .D3(DBUSTOREGIN[3]), .D4(bussplitter_1_d4), .D5(bussplitter_1_d5), .D6(bussplitter_1_d6),
    .D7(bussplitter_1_d7));
  assign MICRO[0] = OE_ROM ? dPRG__MICRO[0] : 1'bz;  // Driver driver_23
  LED led_43 (.in(dPRG__MICRO[0]));
  D_FF d_ff_8 (.D(d_ff_8_nq), .C(button_8_out), .Q(dPRG__MICRO[0]), .nQ(d_ff_8_nq));
  Button button_8 (.out(button_8_out));
  // _74173 RC: pin names not known; wires that end beside it: nRCLE, CLK, DBUSTOREGIN[3], DBUSTOREGIN[2], DBUSTOREGIN[1], RST, RC[3], 1'b0, RC[2], 1'b1, RC[1], DBUSTOREGIN[0], RC[0]
  assign MUX2_p9[0] = not_16_out ? RC[0] : 1'bz;  // Driver driver_24
  PullDown pulldown_5 (.out(bussplitter_1_d7));
  PullDown pulldown_6 (.out(bussplitter_1_d6));
  PullDown pulldown_7 (.out(bussplitter_1_d5));
  PullDown pulldown_8 (.out(bussplitter_1_d4));
  Seven_Seg_Hex seven_seg_hex_15 (.d(dPRG__HiNB), .dp(1'b0));
  // _74244 BUFFER_2: pin names not known; wires that end beside it: OPR[0], nROMOE, OPR[1], OPR[2], OPR[3], MUX2_p9[0], nENDATABUSTOREGIN, MUX2_p9[1], MUX2_p9[2], MUX2_p9[3], 1'b1, 1'b0, MUX2_p9[0], MUX2_p9[1], MUX2_p9[2], MUX2_p9[3], DBUSTOREGIN[0], DBUSTOREGIN[1], DBUSTOREGIN[2], DBUSTOREGIN[3]
  not not_16 (not_16_out, nRCOE);
  Seven_Seg_Hex seven_seg_hex_16 (.d(dPRG__MICRO), .dp(1'b0));
  Button STEP_float (.out(Stepf));
  Seven_Seg_Hex seven_seg_hex_17 (.d(dPRG__MAddr), .dp(1'b0));
  Seven_Seg_Hex seven_seg_hex_18 (.d(dPRG__OPR), .dp(1'b0));
  PullUp pullup_5 (.out(pullup_5_out));
  assign MAddr[3] = OE_ROM ? dPRG__MAddr[3] : 1'bz;  // Driver driver_25
  LED led_44 (.in(dPRG__MAddr[3]));
  D_FF d_ff_9 (.D(d_ff_9_nq), .C(button_9_out), .Q(dPRG__MAddr[3]), .nQ(d_ff_9_nq));
  not not_17 (not_17_out, MICRO[3]);
  // SwitchDT Program: pin names not known; wires that end beside it: MICRO2_IN, pullup_5_out, Program_p3
  // _7432 _7432_1: pin names not known; wires that end beside it: nACCTOALU, nMD0, nACCTOALU, nMD1, nACCTOALU, nMD2, nACCTOALU, nMD3, 1'b1, 1'b0, nACCn, nACCRA, nACCRB, nACCRAM
  assign MAddr[2] = OE_ROM ? dPRG__MAddr[2] : 1'bz;  // Driver driver_26
  LED led_45 (.in(dPRG__MAddr[2]));
  D_FF d_ff_10 (.D(d_ff_10_nq), .C(button_10_out), .Q(dPRG__MAddr[2]), .nQ(d_ff_10_nq));
  Button button_9 (.out(button_9_out));
  DiodeForward diodeforward_1 (.in(I0), .out(nLDIACCn));
  DiodeForward diodeforward_2 (.in(nMD0), .out(nLDIACCn));
  DiodeForward diodeforward_3 (.in(I0), .out(diodeforward_3_out));
  DiodeForward diodeforward_4 (.in(nMD1), .out(diodeforward_3_out));
  DiodeForward diodeforward_5 (.in(I0), .out(diodeforward_5_out));
  DiodeForward diodeforward_6 (.in(nMD2), .out(diodeforward_5_out));
  DiodeForward diodeforward_7 (.in(I0), .out(diodeforward_7_out));
  DiodeForward diodeforward_8 (.in(nMD3), .out(diodeforward_7_out));
  DiodeForward diodeforward_9 (.in(I7), .out(diodeforward_9_out));
  DiodeForward diodeforward_10 (.in(nMD1), .out(diodeforward_9_out));
  DiodeForward diodeforward_11 (.in(I7), .out(diodeforward_11_out));
  DiodeForward diodeforward_12 (.in(nMD2), .out(diodeforward_11_out));
  DiodeForward diodeforward_13 (.in(I7), .out(diodeforward_13_out));
  DiodeForward diodeforward_14 (.in(nMD3), .out(diodeforward_13_out));
  DiodeForward diodeforward_15 (.in(I3), .out(diodeforward_15_out));
  DiodeForward diodeforward_16 (.in(nMD1), .out(diodeforward_15_out));
  DiodeForward diodeforward_17 (.in(I3), .out(diodeforward_17_out));
  DiodeForward diodeforward_18 (.in(nMD2), .out(diodeforward_17_out));
  DiodeForward diodeforward_19 (.in(I3), .out(nRCOE));
  DiodeForward diodeforward_20 (.in(nMD3), .out(nRCOE));
  assign MAddr[1] = OE_ROM ? dPRG__MAddr[1] : 1'bz;  // Driver driver_27
  LED led_46 (.in(dPRG__MAddr[1]));
  D_FF d_ff_11 (.D(d_ff_11_nq), .C(button_11_out), .Q(dPRG__MAddr[1]), .nQ(d_ff_11_nq));
  Button button_10 (.out(button_10_out));
  // _74138 _74138_1: pin names not known; wires that end beside it: MICRO[0], MICRO[2], MICRO[1], not_17_out, Program_p3, Program_p3, 1'b1, 1'b0, I0, I1, I2, I3, I4, I5, I6, I7
  // _74138 _74138_2: pin names not known; wires that end beside it: MICRO[0], MICRO[2], MICRO[1], MICRO[3], Program_p3, Program_p3, 1'b1, 1'b0, I8, I9, I10, I11, I12, I13, I14, I15
  PullDown pulldown_9 (.out(nLDIACCn));
  PullDown pulldown_10 (.out(diodeforward_3_out));
  PullDown pulldown_11 (.out(diodeforward_5_out));
  PullDown pulldown_12 (.out(diodeforward_7_out));
  PullDown pulldown_13 (.out(diodeforward_9_out));
  PullDown pulldown_14 (.out(diodeforward_11_out));
  PullDown pulldown_15 (.out(diodeforward_13_out));
  PullDown pulldown_16 (.out(diodeforward_15_out));
  PullDown pulldown_17 (.out(diodeforward_17_out));
  PullDown pulldown_18 (.out(nRCOE));
  nand nand_5 (nand_5_out, CARRY, JPC);
  nand nand_6 (nand_6_out, ZERO, JPZ);
  assign MAddr[0] = OE_ROM ? dPRG__MAddr[0] : 1'bz;  // Driver driver_28
  LED led_47 (.in(dPRG__MAddr[0]));
  D_FF d_ff_12 (.D(d_ff_12_nq), .C(button_12_out), .Q(dPRG__MAddr[0]), .nQ(d_ff_12_nq));
  Button button_11 (.out(button_11_out));
  LED led_48 (.in(dPRG__OPR[3]));
  Button button_12 (.out(button_12_out));
  and and_10 (and_10_out, diodeforward_3_out, diodeforward_5_out);
  and and_11 (nRALE, diodeforward_3_out, diodeforward_9_out);
  and and_12 (nRBLE, diodeforward_5_out, diodeforward_11_out);
  and and_13 (nRCLE, diodeforward_7_out, diodeforward_13_out);
  and and_14 (and_14_out, nACCRA, diodeforward_15_out);
  and and_15 (nRBOE, nACCRB, diodeforward_17_out);
  and and_16 (nLOADADDRC, nand_5_out, nand_6_out);
  assign OPR[3] = OE_ROM ? dPRG__OPR[3] : 1'bz;  // Driver driver_29
  LED led_49 (.in(dPRG__OPR[2]));
  D_FF d_ff_13 (.D(d_ff_13_nq), .C(button_13_out), .Q(dPRG__OPR[3]), .nQ(d_ff_13_nq));
  Button button_13 (.out(button_13_out));
  and and_17 (and_17_out, and_10_out, diodeforward_7_out);
  assign OPR[2] = OE_ROM ? dPRG__OPR[2] : 1'bz;  // Driver driver_30
  LED led_50 (.in(dPRG__OPR[1]));
  D_FF d_ff_14 (.D(d_ff_14_nq), .C(button_14_out), .Q(dPRG__OPR[2]), .nQ(d_ff_14_nq));
  Button button_14 (.out(button_14_out));
  DiodeBackward diodebackward_3 (.in(and_17_out), .out(nDATATOREG));
  DiodeBackward diodebackward_4 (.in(DATATOREG2), .out(nDATATOREG));
  DiodeBackward diodebackward_5 (.in(and_14_out), .out(nRAOE));
  DiodeBackward diodebackward_6 (.in(nOUTxRA), .out(nRAOE));
  assign OPR[1] = OE_ROM ? dPRG__OPR[1] : 1'bz;  // Driver driver_31
  LED led_51 (.in(dPRG__OPR[0]));
  D_FF d_ff_15 (.D(d_ff_15_nq), .C(button_15_out), .Q(dPRG__OPR[1]), .nQ(d_ff_15_nq));
  Button button_15 (.out(button_15_out));
  PullUp pullup_6 (.out(nDATATOREG));
  PullUp pullup_7 (.out(nRAOE));
  not not_18 (nWE_ROM, OE_ROM);
  DipSwitch SEL__Prog (.out(OE_ROM));
  assign OPR[0] = OE_ROM ? dPRG__OPR[0] : 1'bz;  // Driver driver_32
  D_FF d_ff_16 (.D(d_ff_16_nq), .C(button_16_out), .Q(dPRG__OPR[0]), .nQ(d_ff_16_nq));
  Button button_16 (.out(button_16_out));
  not not_19 (not_19_out, nRE);
  not not_20 (not_20_out, MICRO2_IN);
  // _7432 _7432_2: pin names not known; wires that end beside it: nOUTx, nMD0, nOUTx, nMD2, nOUTx, nMD3, not_19_out, nDATATOREG, 1'b1, 1'b0, nOUTxn, nOUTxRA, nOUTxRAM, nENDATABUSTOREGIN
  // _74139 _74139_1: pin names not known; wires that end beside it: MOD0, MOD1, not_20_out, MOD0, MOD1, 1'b0, 1'b1, 1'b0, nINAOE, nINBOE, nINCOE, nINDOE, nMD0, nMD1, nMD2, nMD3
  DiodeBackward diodebackward_7 (.in(nOUTxRAM), .out(nSOURCEB));
  DiodeBackward diodebackward_8 (.in(nACCRAM), .out(nSOURCEB));
  nand nand_7 (nACCTOREGIN, nDATATOREG, nRE);
  PullUp pullup_8 (.out(nSOURCEB));
  DiodeBackward diodebackward_9 (.in(nOUTxn), .out(DATATOREG2));
  DiodeBackward diodebackward_10 (.in(nOUTxRA), .out(DATATOREG2));
  DiodeBackward diodebackward_11 (.in(nOUTxRAM), .out(DATATOREG2));
  PullUp pullup_9 (.out(DATATOREG2));
  DiodeBackward diodebackward_12 (.in(nINAOE), .out(nINxOE));
  DiodeBackward diodebackward_13 (.in(nINBOE), .out(nINxOE));
  PullUp pullup_10 (.out(nINxOE));
  DiodeBackward diodebackward_14 (.in(nINCOE), .out(nINxOE));
  DiodeBackward diodebackward_15 (.in(nINDOE), .out(nINxOE));
  DiodeBackward diodebackward_16 (.in(I0), .out(nROMOE));
  DiodeBackward diodebackward_17 (.in(nACCn), .out(nROMOE));
  DiodeBackward diodebackward_18 (.in(nOUTxn), .out(nROMOE));
  DiodeBackward diodebackward_19 (.in(nLDIACCn), .out(nCLOCKACCEN));
  DiodeBackward diodebackward_20 (.in(nINxOE), .out(nCLOCKACCEN));
  DiodeBackward diodebackward_21 (.in(I1), .out(nCLOCKACCEN));
  DiodeBackward diodebackward_22 (.in(I2), .out(nCLOCKACCEN));
  DiodeBackward diodebackward_23 (.in(I3), .out(nCLOCKACCEN));
  DiodeBackward diodebackward_24 (.in(I8), .out(nCLOCKACCEN));
  DiodeBackward diodebackward_25 (.in(I11), .out(nCLOCKACCEN));
  DiodeBackward diodebackward_26 (.in(I15), .out(nCLOCKACCEN));
  DiodeBackward diodebackward_27 (.in(I1), .out(nACCTOALU));
  DiodeBackward diodebackward_28 (.in(I8), .out(nACCTOALU));
  DiodeBackward diodebackward_29 (.in(I11), .out(nACCTOALU));
  DiodeBackward diodebackward_30 (.in(I15), .out(nACCTOALU));
  DiodeBackward diodebackward_31 (.in(I4), .out(nOUTx));
  DiodeBackward diodebackward_32 (.in(I5), .out(nOUTx));
  DiodeBackward diodebackward_33 (.in(I6), .out(nOUTx));
  DiodeBackward diodebackward_34 (.in(I9), .out(nOUTx));
  not not_21 (JPC, I13);
  not not_22 (JPZ, I14);
  not not_23 (ARITH__nNAND, I1);
  or or_7 (nWE, CLKN, I10);
  and and_18 (nRE, I2, nSOURCEB);
  PullUp pullup_11 (.out(nROMOE));
  PullUp pullup_12 (.out(nCLOCKACCEN));
  PullUp pullup_13 (.out(nACCTOALU));
  PullUp pullup_14 (.out(nOUTx));

  // Other names for the same wires on the sheet: PRGDataMICRO1[7:0] = {MAddr, OPR};
  //   PRGDataMICRO2[7:0] = {MICRO2_IN, AMODE, MOD1, MOD0, MICRO}; RAM__DATA[3:0] = DBUSTOREGIN; nADD = I15;
  //   nARITH__NAND = I1; nCMP = I8; nJPC = I13; nJPI = I12; nJPZ = I14; nLDA = I3; nLDI = I0; nLDR = I7; nLDW = I2;
  //   nOUTALE = I4; nOUTBLE = I5; nOUTCLE = I6; nOUTDLE = I9; nSTW = I10; nSUB = I11

  // Notes on the sheet:
  //   -
  //   MikroLeo
  //   A 4-bit didactic Microcomputer without a microprocessor.
  //   Made by classical 74xxx family integrated circuits.
  //   Designed by: Edson Junior Acordi
  //   First release: (April-2020)
  //   Last release: v0.19 (Fev-2021)
  //   OUTD
  //   Instructions
  //   ~LDI
  //   ~JPZ
  //   ~NAND
  //   ~ADD
  //   OUTC
  //   ~LDW
  //   OUTB
  //   ~LDA
  //   Clock Circuit
  //   Conditional jump (short, JPC and JPZ):
  //   PC <= MA[7:4]:LA[3:0]
  //   PCH = PCH (not modified)
  //   (256 word pages)
  //   Unconditional jump (long, JPI):
  //   PC = RC:MA[7:4]:LA[3:0]
  //   PCH <= RC
  //   (all memory addresses)
  //   RAM DATA=>
  //   ~OUTA
  //   OUTA
  //   ~OUTB
  //   ~OUTC
  //   The bit AMODE, selects the Addressing Mode.
  //   The adderssing modes are valid for data addressing
  //    and jumps.
  //   If AMODE=0, Indirect + immediate addressing mode
  //   if AMODE=1, Register Indirect addressing mode
  //   Register indirect + Immediate => Address=[RC:MAddr:LAddr]
  //   Register indirect => Address=[RC:RB:RA]
  //   ~LDR
  //   7408
  //   7404
  //   Reset Circuit
  //   Note: when establishing the power supply, the ~RSTPC signal must stay
  //   briefly at 0, to perform the reset (PWONRST).
  //   Addressing Modes
  //   ACC
  //   ~CMP
  //   INPUT PORTS
  //   ~INA
  //   Holds the signal ~LD until data Load finish
  //   Allows that in the jump instructions, the PC
  //   keep the ~LD signal active for a while larger
  //   so that the load of the data containing the
  //   address be possible. After the load, the
  //   ~LOADADDRC or ~JPI signal (stored in Latch
  //   7474), returns to "1".
  //   Data loading is synchronized way with the
  //   clock signal.
  //   Note: FF must be started with Q=1.
  //   Timing for Branches Instructions.
  //   Panel Debug
  //   ~OUTD
  //   ~INB
  //   7432
  //   Reset manual
  //   RC
  //   ~STW
  //   ~INC
  //   Inverter and Delay
  //   ~SUB
  //   ~IND
  //   RB
  //   ~JPI
  //   FLAGS
  //   CARRY
  //   RA
  //   ~JPC
  //   ZERO
  //   $OSHW$
  //   2k (ROM) / 2k word (RAM)
  //   Arithmetic and Logic Unit (ALU)
  //   DATABUS =>
  //   Input Ports
  //   INA
  //   INB
  //   INC
  //   IND
  //   Program Counter
  //   PCH
  //   MICRO2
  //   ROM
  //   Some Control Signals
  //   Program Counter (PC)
  //   AMODE
  //   Complement of B input
  //   ~SUB/ADD=1 and ~CMP=1, SUM Operatin
  //   ~SUB/ADD=0 and ~CMP=1, SUBTRACTION Operation
  //   ~SUB/ADD=1 and ~CMP=0, COMPARISON Operation
  //   If S = 0, ALU input B receives RAM[Addr]
  //   If S = 1, ALU input B receives DataBus
  //   Allows use of NAND, CMP, SUB instructions
  //   and ADD between ACC and memory.
  //   PCM
  //   Instruction Word
  //   CONTROL REGISTERS
  //   PCL
  //   Modifier
  //   The PC (74161) is incremented
  //   in the transition from 0 to 1.
  //   The ~LD works synchronously
  //   with the clock input.
  //   Opcode
  //   7486
  //   MAddr
  //   ~Read
  //   ~Write
  //   RAM
  //   Cin
  //   REG_IN
  //   Operand
  //   BUS
  //   Address
  //   Logic Operation
  //   Flags Register
  //   <= ACC
  //   Delay
  //   Manual Programming Interface
  //   SEL Prog:
  //   Position 0 = Read RAM Data (Run Program)
  //   Position 1 = Write RAM Data
  //   Program Memory (ROM) - 2k x 16
  //   7400
  //   74244
  //   DataBus
  //   contents of Micro1 (hex, n*v repeats v):
  //   a,b,c,d,e,f,1,2,3,4,5,6,7,8,9,a,0,0,0,0,1,0,2,0,2,0,3,0,3,0,4,0,4,0,5,0,6,0,0,0,9,
  //   7,0,7,a,8,0,8,c,f,0,f,f,8,0,7
  //   contents of Micro2 (hex, n*v repeats v):
  //   4,5,6,9,4,5,6,9,4,5,6,9,4,5,6,9,4,5,6,9,0,14,10,24,0,15,10,25,0,16,10,26,0,19,10,
  //   29,0,a,0,34,0,a,0,35,0,a,0,36,0,a,0,39,34,35,36,39,4,5,6,9
  //   Implemented with two RAM 6116.
  //   MODIFIER
  //   IN/AddressM
  //   RAM 2k x 4 (IDT6116)
  //   Operand n
  //   (Low Address)
  //   (Median Address)
  //   (OPCODE)
  //   Buffer OPERAND to DataBus
  //   Connect the Operand to the DataBus.
  //   Connects the DataBus to the Registers input.
  //   Detector of ZERO
  //   (High Address)
  //   <= DATABUS to REG_{IN}
  //   HiNB
  //   Buffer DataBus to REG_IN
  //   <= DATABUS
  //   Registers
  //   DATA <=>
  //   MICRO
  //   DATA =>
  //   OPR
  //   <= DATA
  //   Instruction Decoder (ID)
  //   The "Program" switch disables MICRODE1
  //   when in the pull-up resistor position.
  //   Used to program memory program.
  //   Control Unit (UC)
  //   It generates the signals for the execution of the LDI, LDR and LDA
  //   Instruction.
  //   Signals Generation for execution of ADD, SUB, NAND and CMP
  //   Instructions.
  //   Generation of ~LOADADDRC signal (short conditional jumps - PCM and PCL, +- 128  positions)
  //   LDI ACC,n
  //   OR gate
  //   LDI RA,n
  //   LDI RB,n
  //   LDI RD,n
  //   LDR RA
  //   LDR RB
  //   LDR RD
  //   LDA RA
  //   LDA RB
  //   LDA RD
  //   NAND ACC,n / ADD ACC,n / SUB ACC,n / CMP ACC, n
  //   NAND ACC,RA / ADD ACC,RA / SUB ACC,RA / CMP ACC,RA
  //   NAND ACC,RB / ADD ACC,RB / SUB ACC,RB / CMP ACC,RB
  //   NAND ACC,RAM[n] / ADD ACC,RAM[n] / SUB ACC,RAM[n] / CMP ACC,RAM[n]
  //   AND gate
  //   LDI(0)
  //   NAND(1)
  //   LDW(2)
  //   LDA(3)
  //   OUTA(4)
  //   OUTB(5)
  //   OUTC(6)
  //   LDR(7)
  //   CMP(8)
  //   OUTD(9)
  //   STW(A)
  //   SUB(B)
  //   JPI(C)
  //   JPC(D)
  //   JPZ(E)
  //   ADD(F)
  //   Generation of signals for execution of instructions OUTA,
  //   OUTB, OUTC e OUTD
  //   Note: The ~ACCTOREGIN signal is used to execute the 'OUTx ACC' instruction.
  //   Generation of the ~ENDATABUSTOREGIN signal.
  //   Decoding of MDx and INxOE signals for the execution of
  //   Instructions, LDI/LDA/LDR, NAND/SUB/ADD/CMP, OUTx or INx.
  //   ~INx is needed because the instructions
  //   INx are not decoded by ID.
  //   MOD0 (previous name: STLD0)
  //   MOD1 (previous name: STLD1)
  //   Enables reading from RAM and directs ALU input B to receive the value from
  //   RAM in Arithmetic/Logic operations that use RAM.
  //   Generation of the ~ACCTOREGIN Signal
  //   The ~DATATOREG, ~SOURCEB, and ~LDW signals disable the ~ACCTOREGIN signal.
  //   ~OUTX
  //   OUTx => OUTA / OUTB / OUTC / OUTD
  //   OUTx n
  //   OUTx RA
  //   OUTx RAM[n]
  //   When the circuit is turned on, the CLK clock signal
  //   initializes in logic 0 state.
  //   In this state, the code to be executed is read from
  //   program memory and all control signals are generated.
  //   It is important that all control signals are generated
  //   before the clock pulse occurs.
  //   In addition, it is important that all the data needed to
  //   execute the instruction is also available before the
  //   clock pulse occurs.
  //   The program counter (PC) must be the last to be
  //   incremented. The PC (74161) is incremented on the
  //   falling edge of the clock signal.
  //   Therefore, the Clock signal used on the PC is CLKN.
  //   So, only after executing the first instruction the PC
  //   will be incremented.
  //   CPU Phases:
  //   CLK_{----------}|^{----------}|_{----------}
  //   $$ $$ $$ $$ $$ph_1$$ $$ ph_2$$ $$ $$ph_3
  //   Phase 1 (ph1): the word code (HiNB, Opcode, MAddr
  //   and operand) is read from the program memory and
  //   the respective control signals are generated.
  //   Phase 2 (ph2): On the rising edge of the CLK clock
  //   signal the instruction is executed.
  //   Phase 3 (ph3): On the falling edge of the CLK clock
  //   signal the program counter is incremented.
  //   CLKN => Fetch of Instruction/decode
  //   CLK => execute
  //   Signals to modify the font of
  //   data in the LDA / LDR Instructions,
  //   NAND / SUB / ADD / CMP, or the
  //   data destination in the LDI instruction:
  //   ~MD0 (previous name: LD0)
  //   ~MD1 (previous name: LD1)
  //   ~MD2 (previous name: LD2)
  //   ~MD3 (previous name: LD3)
  //   Generation of ~ROMOE signal
  //   Generation of ~CLOCKACCEN signal
  //   Generation of ~ACCTOALU signal
  //   Generation of ~OUTx signal
  //   Generation of JPC and JPZ signal
  //   Generation of ~ARITH\_LOGIC signal
  //   Generation of ~RE and ~WE Signals
  //   AND gate with diodes
  //   ~ENDATABUSTOREGIN
  //   ~CLOCKACCE
  //   ~ARITH\_LOGIC
  //   ~ACCTOREGIN
  //   ~ACCTOALU
endmodule
